# Fritzing sketch SmacSchema (saved by Fritzing 0.9.2b)
breadboards: 1

parts:
  DHT1 = DHT11 Humitidy and Temperature Sensor
  DHT2 = DHT11 Humitidy and Temperature Sensor
  R1 = Resistor [tolerance=±5% resistance=4.7k package="2512 [SMD]"]
  R2 = Resistor [tolerance=±5% resistance=470 package="2512 [SMD]"]
  R3 = Resistor [tolerance=±5% resistance=470 package="2512 [SMD]"]
  Raspberry_Pi1 = Raspberry Pi 2
  R4 = Resistor [tolerance=±5% resistance=2.2k package=THT]
  R5 = Resistor [tolerance=±5% resistance=10k package=THT]
  KY-2 = Keyes Relay [package=THT]
  Q1 = NPN-Transistor [package="TO92 [THT]"]
  DHT3 = DHT11 Humitidy and Temperature Sensor

nets:
  5V: DHT1.VDD, DHT2.VDD, Raspberry_Pi1.3v3, DHT3.VDD
  N1: DHT1.DATA, R1.Pin_0
  GND: DHT1.GND, DHT2.GND, Raspberry_Pi1.GND, R5.Pin_1, KY-2.ground, Q1.E, DHT3.GND
  N2: DHT2.DATA, R2.Pin_0
  N3: R1.Pin_1, Raspberry_Pi1.GPIO15
  N4: R2.Pin_1, Raspberry_Pi1.GPIO17
  N5: R3.Pin_0, DHT3.DATA
  N6: R3.Pin_1, Raspberry_Pi1.GPIO27
  N7: Raspberry_Pi1.GPIO20, R4.Pin_1, R5.Pin_0
  N8: Raspberry_Pi1.5V, KY-2.power
  N9: R4.Pin_0, Q1.B
  N10: KY-2.signal, Q1.C
  N11: KY-2.NC, KY-2.C, KY-2.NO

custom parts:
  DHT11 Humitidy and Temperature Sensor: DHT11 Humidity and Temperature Sensor
  Keyes Relay: The Keyes 5V relay module is suitable for SCM development, home appliance control. It uses a 5V~12V TIL control signal which can control DC / AC signal.
